# Fritzing sketch normal_push (saved by Fritzing 0.8.7b)
breadboards: 1

parts:
  Part1 = Arduino Uno (Rev3)
  S1 = Pushbutton [package="[THT]"]
  LED1 = LED - 5mm [color="Red (633nm)" package="5 mm [THT]"]
  R1 = Resistor [tolerance=±5% resistance=10k package=THT]
  R2 = Resistor [package="2512 [SMD]"]

nets:
  N1: Part1.D13/SCK, Part1.5V, S1.Pin_1, S1.Pin_2, S1.Pin_3, S1.Pin_4, R1.Pin_0
  N2: Part1.D7, R2.Pin_1
  N3: Part1.GND, LED1.cathode, R1.Pin_1
  N4: LED1.anode, R2.Pin_0
